// Logisim project MIPS_Pipeline.circ as structural Verilog: 20 circuits, main circuit ALU
module ALU (
  input  [2:0] ALUOp,
  input  [15:0] Operand1,
  input  [15:0] Operand2,
  input  [2:0] Shamt,
  output [15:0] Result
);

  wire equal_checker_16bit_1_zero;
  wire [0:0] subtractor_1_out_2;
  wire [14:0] subtractor_1_out;
  wire [15:0] adder_1_out, and_1_out, or_1_out, shifter_1_out, shifter_2_out;

  Adder #(.width(16)) adder_1 (.a(Operand1), .b(Operand2), .out(adder_1_out));  // open: cin, cout
  Subtractor #(.width(16)) subtractor_1 (
    .a(Operand1), .b(Operand2), .out({subtractor_1_out_2[0], subtractor_1_out}));  // open: bin, bout
  assign and_1_out = Operand1 & Operand2;  // AND_Gate and_1, 16 bits wide
  assign or_1_out = Operand1 | Operand2;  // OR_Gate or_1, 16 bits wide
  Shifter #(.width(16)) shifter_1 (.in(Operand1), .\dist ({1'b0, Shamt}), .out(shifter_1_out));
  Shifter #(.shift("lr"), .width(16)) shifter_2 (.in(Operand1), .\dist ({1'b0, Shamt}), .out(shifter_2_out));
  Multiplexer #(.select(3), .width(16)) multiplexer_1 (
    .in0(adder_1_out), .in1({subtractor_1_out_2[0], subtractor_1_out}), .in2(and_1_out), .in3(or_1_out),
    .in4(shifter_1_out), .in5(shifter_2_out), .in6({{15{1'b0}}, subtractor_1_out_2[0]}), .out(Result),
    .sel(ALUOp));  // open: in7
  Equal_Checker_16bit equal_checker_16bit_1 (
    .bits({subtractor_1_out_2[0], subtractor_1_out}), .Zero(equal_checker_16bit_1_zero));
endmodule

module Equal_Checker_16bit (
  input  [15:0] bits,
  output Zero
);

  wire or_1_out;

  or or_1 (or_1_out, bits[0], bits[1], bits[2], bits[3], bits[4], bits[5], bits[6], bits[7], bits[9], bits[10], bits[11], bits[12], bits[13], bits[14], bits[15], bits[8]);
  not not_1 (Zero, or_1_out);
endmodule

module Registers (
  input  RegWrite,
  input  [2:0] ReadAddress1,
  input  [2:0] ReadAddress2,
  input  [2:0] WriteAddress,
  input  [15:0] Data_Input,
  input  Clk,
  output [15:0] RegData1,
  output [15:0] RegData2,
  output [15:0] zero,
  output [15:0] r0,
  output [15:0] r1,
  output [15:0] r2,
  output [15:0] r3,
  output [15:0] r4,
  output [15:0] r5,
  output [15:0] ra
);

  wire demultiplexer_1_out0, demultiplexer_1_out1, demultiplexer_1_out2, demultiplexer_1_out3,
       demultiplexer_1_out4, demultiplexer_1_out5, demultiplexer_1_out6, demultiplexer_1_out7;

  Demultiplexer #(.select(3)) demultiplexer_1 (
    .out0(demultiplexer_1_out0), .out1(demultiplexer_1_out1), .out2(demultiplexer_1_out2),
    .out3(demultiplexer_1_out3), .out4(demultiplexer_1_out4), .out5(demultiplexer_1_out5),
    .out6(demultiplexer_1_out6), .out7(demultiplexer_1_out7), .in(RegWrite), .sel(WriteAddress));
  Register #(.width(16)) register_1 (.D(Data_Input), .en(demultiplexer_1_out0), .Q(zero), .clk(Clk));  // open: clr
  Register #(.width(16)) register_2 (.D(Data_Input), .en(demultiplexer_1_out1), .Q(r0), .clk(Clk));  // open: clr
  Register #(.width(16)) register_3 (.D(Data_Input), .en(demultiplexer_1_out2), .Q(r1), .clk(Clk));  // open: clr
  Register #(.width(16)) register_4 (.D(Data_Input), .en(demultiplexer_1_out3), .Q(r2), .clk(Clk));  // open: clr
  Register #(.width(16)) register_5 (.D(Data_Input), .en(demultiplexer_1_out4), .Q(r3), .clk(Clk));  // open: clr
  Register #(.width(16)) register_6 (.D(Data_Input), .en(demultiplexer_1_out5), .Q(r4), .clk(Clk));  // open: clr
  Register #(.width(16)) register_7 (.D(Data_Input), .en(demultiplexer_1_out6), .Q(r5), .clk(Clk));  // open: clr
  Register #(.width(16)) register_8 (.D(Data_Input), .en(demultiplexer_1_out7), .Q(ra), .clk(Clk));  // open: clr
  Multiplexer #(.select(3), .width(16)) multiplexer_1 (
    .in0(zero), .in1(r0), .in2(r1), .in3(r2), .in4(r3), .in5(r4), .in6(r5), .in7(ra), .out(RegData1),
    .sel(ReadAddress1));
  Multiplexer #(.select(3), .width(16)) multiplexer_2 (
    .in0(zero), .in1(r0), .in2(r1), .in3(r2), .in4(r3), .in5(r4), .in6(r5), .in7(ra), .out(RegData2),
    .sel(ReadAddress2));
endmodule

module MIPS_Single_Cycle (
  output [15:0] zero,
  output [15:0] r0,
  output [15:0] r1,
  output [15:0] r2,
  output [15:0] r3,
  output [15:0] r4,
  output [15:0] r5,
  output [15:0] ra
);

  wire alu_1_p5, and_1_out, clock_1_out, control_1_p2, control_1_p3, control_1_p4, control_1_p5,
       control_1_p6, control_1_p7, control_1_p8, control_1_p9, control_1_p10, control_1_p11, control_1_p12,
       control_1_p13, multiplexer_7_out, not_1_out, rom_enable_1_enable;
  wire [2:0] multiplexer_1_out, multiplexer_3_out;
  wire [3:0] adder_1_out;
  wire [11:0] adder_1_out_2;
  wire [15:0] adder_2_out, alu_1_p6, multiplexer_2_out, multiplexer_4_out, multiplexer_5_out,
       multiplexer_6_out, multiplexer_8_out, multiplexer_9_out, ram_1_dout, register_1_q,
       registers_1_regdata1, registers_1_regdata2, rom_1_data, sign_extend_1_out_2;

  Clock clock_1 (.out(clock_1_out));
  Register #(.width(16)) register_1 (.D(multiplexer_8_out), .Q(register_1_q), .clk(clock_1_out));  // open: en, clr
  ROM #(.addrWidth(16), .dataWidth(16)) rom_1 (.addr(register_1_q), .data(rom_1_data));
  Adder #(.width(16)) adder_1 (.a(register_1_q), .b(16'h1), .out({adder_1_out, adder_1_out_2}));  // open: cin, cout
  // Control control_1: pin names not known; wires that end beside it: rom_1_data, control_1_p2, control_1_p3, control_1_p4, control_1_p5, control_1_p6, control_1_p7, control_1_p8, control_1_p9, control_1_p10, control_1_p11, control_1_p12, control_1_p13
  Multiplexer #(.width(3)) multiplexer_1 (
    .in0(rom_1_data[8:6]), .in1(3'b111), .out(multiplexer_1_out), .sel(control_1_p13));
  Multiplexer #(.width(16)) multiplexer_2 (
    .in0(multiplexer_9_out), .in1({adder_1_out, adder_1_out_2}), .out(multiplexer_2_out), .sel(control_1_p13));
  Multiplexer #(.width(3)) multiplexer_3 (
    .in0(multiplexer_1_out), .in1(rom_1_data[5:3]), .out(multiplexer_3_out), .sel(control_1_p12));
  Registers registers_1 (
    .Clk(clock_1_out), .RegWrite(control_1_p11), .ReadAddress1(rom_1_data[11:9]),
    .ReadAddress2(rom_1_data[8:6]), .WriteAddress(multiplexer_3_out), .Data_Input(multiplexer_2_out),
    .zero(zero), .r0(r0), .r1(r1), .r2(r2), .r3(r3), .r4(r4), .r5(r5), .ra(ra),
    .RegData1(registers_1_regdata1), .RegData2(registers_1_regdata2));
  Sign_Extend sign_extend_1 (.in_1(rom_1_data[5:0]), .out_2(sign_extend_1_out_2));
  Multiplexer #(.width(16)) multiplexer_4 (
    .in0({adder_1_out, rom_1_data[11:0]}), .in1(registers_1_regdata1), .out(multiplexer_4_out),
    .sel(control_1_p2));
  Multiplexer #(.width(16)) multiplexer_5 (
    .in0(registers_1_regdata2), .in1(sign_extend_1_out_2), .out(multiplexer_5_out), .sel(control_1_p10));
  not not_1 (not_1_out, alu_1_p5);
  // ALU alu_1: pin names not known; wires that end beside it: registers_1_regdata1, multiplexer_5_out, rom_1_data[8:6], control_1_p9, alu_1_p5, alu_1_p6
  Multiplexer #(.width(16)) multiplexer_6 (
    .in0({adder_1_out, adder_1_out_2}), .in1(adder_2_out), .out(multiplexer_6_out), .sel(and_1_out));
  Adder #(.width(16)) adder_2 (
    .a({adder_1_out, adder_1_out_2}), .b(sign_extend_1_out_2), .out(adder_2_out));  // open: cin, cout
  Multiplexer multiplexer_7 (.in0(alu_1_p5), .in1(not_1_out), .out(multiplexer_7_out), .sel(control_1_p3));
  and and_1 (and_1_out, multiplexer_7_out, control_1_p4);
  RAM #(.addrWidth(16), .dataWidth(16), .trigger("falling")) ram_1 (
    .addr(alu_1_p6), .we(control_1_p7), .oe(control_1_p8), .clk(rom_enable_1_enable),
    .din(registers_1_regdata2), .dout(ram_1_dout));
  ROM_Enable rom_enable_1 (.Write(clock_1_out), .Read(control_1_p8), .Clk(control_1_p7), .Enable(rom_enable_1_enable));
  Multiplexer #(.width(16)) multiplexer_8 (
    .in0(multiplexer_6_out), .in1(multiplexer_4_out), .out(multiplexer_8_out), .sel(control_1_p5));
  Multiplexer #(.disabled("Z"), .width(16)) multiplexer_9 (
    .in0(alu_1_p6), .in1(ram_1_dout), .out(multiplexer_9_out), .sel(control_1_p6));

  // Notes on the sheet:
  //   contents of rom_1 (hex, n*v repeats v):
  //   105e 109f 10c0 1141 572 4c01 658 24c 455 5439 30c0
endmodule

module Control (
  input  [15:0] Opcode,
  output Jr,
  output BranchNe,
  output Branch,
  output Jump,
  output MemtoReg,
  output MemWrite,
  output MemRead,
  output ALUSrc,
  output RegWrite,
  output RegDst,
  output Jal,
  output [2:0] ALUOp
);

  wire control_nope_1_nope, opcode_decoder_1_funct;
  wire [2:0] alu_decoder_1_aluop;

  Control_Nope control_nope_1 (.Instruction(Opcode), .Nope(control_nope_1_nope));
  Opcode_Decoder opcode_decoder_1 (
    .Nope(control_nope_1_nope), .Opcode(Opcode[15:12]), .Funct(opcode_decoder_1_funct), .Jr(Jr),
    .BranchNe(BranchNe), .Branch(Branch), .Jump(Jump), .MemtoReg(MemtoReg), .MemWrite(MemWrite),
    .MemRead(MemRead), .ALUSrc(ALUSrc), .RegWrite(RegWrite), .RegDst(RegDst), .Jal(Jal));
  ALU_Decoder alu_decoder_1 (.Opcode(Opcode[15:12]), .ALUOp(alu_decoder_1_aluop));
  Multiplexer #(.width(3)) multiplexer_1 (
    .in0(alu_decoder_1_aluop), .in1(Opcode[2:0]), .out(ALUOp), .sel(opcode_decoder_1_funct));
endmodule

module PC (
  input  [15:0] OverWrite,
  input  Clk,
  output [15:0] InstructionAddress
);

  Register #(.width(16)) register_1 (.D(OverWrite), .Q(InstructionAddress), .clk(Clk));  // open: en, clr
endmodule

module ALU_Decoder (
  input  [3:0] Opcode,
  output [2:0] ALUOp
);

  wire and_1_out, not_1_out, not_2_out, not_3_out, not_4_out;

  not not_1 (not_1_out, Opcode[3]);
  not not_2 (not_2_out, Opcode[2]);
  not not_3 (not_3_out, Opcode[1]);
  not not_4 (not_4_out, Opcode[0]);
  and and_1 (and_1_out, not_4_out, not_3_out, not_2_out, not_1_out, 1'b0);
  or or_1 (ALUOp[0], and_1_out, Opcode[2]);
  or or_2 (ALUOp[1], and_1_out, and_1_out);
  or or_3 (ALUOp[2], and_1_out, and_1_out);
endmodule

module Opcode_Decoder (
  input  Nope,
  input  [3:0] Opcode,
  output Jr,
  output BranchNe,
  output Branch,
  output Jump,
  output MemtoReg,
  output MemWrite,
  output MemRead,
  output ALUSrc,
  output RegWrite,
  output RegDst,
  output Jal,
  output Funct
);

  wire and_6_out, and_8_out, not_1_out, not_2_out, not_3_out, not_4_out, not_5_out, not_6_out, or_1_out;

  not not_1 (not_1_out, Opcode[3]);
  not not_2 (not_2_out, Opcode[2]);
  not not_3 (not_3_out, Opcode[1]);
  not not_4 (not_4_out, Opcode[0]);
  and and_1 (Jr, not_4_out, Opcode[1], not_2_out, Opcode[3]);
  and and_2 (BranchNe, Opcode[0], not_3_out, Opcode[2], not_1_out);
  not not_5 (not_5_out, Opcode[2]);
  and and_3 (Jal, Opcode[0], not_3_out, not_2_out, Opcode[3]);
  and and_4 (MemWrite, Opcode[0], Opcode[1], not_2_out, not_1_out);
  and and_5 (MemRead, not_4_out, Opcode[1], not_2_out, not_1_out);
  not not_6 (not_6_out, and_6_out);
  and and_6 (and_6_out, not_4_out, not_3_out, not_2_out, not_1_out);
  and and_7 (ALUSrc, not_1_out, not_5_out, not_6_out);
  and and_8 (and_8_out, Opcode[0], not_3_out, not_2_out, not_1_out);
  or or_1 (or_1_out, and_8_out, Jal, MemRead, and_6_out);
  and and_9 (RegWrite, or_1_out, Nope);
  and and_10 (RegDst, Nope, and_6_out);
  and and_11 (Funct, Nope, and_6_out);

  assign Branch = Opcode[2];
  assign Jump = Opcode[3];
  assign MemtoReg = MemRead;
endmodule

module Sign_Extend (
  input  [5:0] in_1,
  output [15:0] out_2
);


  assign out_2 = {{11{in_1[5]}}, in_1[4:0]};
endmodule

module Twos_Complement (
  input  [15:0] in_1,
  output [15:0] out_2
);

  Negator #(.width(16)) negator_1 (.in(in_1), .out(out_2));
endmodule

module ROM_Enable (
  input  Write,
  input  Read,
  input  Clk,
  output Enable
);

  wire and_1_out, and_2_out;

  and and_1 (and_1_out, Write, Clk);
  and and_2 (and_2_out, Read, Clk);
  or or_1 (Enable, and_1_out, and_2_out);
endmodule

module MIPS_Pipeline (
  output [15:0] zero,
  output [15:0] r0,
  output [15:0] r1,
  output [15:0] r2,
  output [15:0] r3,
  output [15:0] r4,
  output [15:0] r5,
  output [15:0] ra
);

  wire Branch_Jump_Stall, clock_1_out, control_1_alusrc, control_1_branch, control_1_branchne, control_1_jal,
       control_1_jr, control_1_jump, control_1_memread, control_1_memtoreg, control_1_memwrite,
       control_1_regdst, control_1_regwrite, equal_checker_branch_1_branch, ex_mem_1_mem_read_out,
       ex_mem_1_mem_to_reg_out, ex_mem_1_mem_write_out, hazard_unit_1_forward_b_id,
       hazard_unit_1_forwards_a_id, hazard_unit_1_stall_ex, hazard_unit_1_stall_id, hazard_unit_1_stall_if,
       id_ex_1_alu_src_out, id_ex_1_mem_read_out, id_ex_1_mem_to_reg_out, id_ex_1_mem_write_out,
       id_ex_1_reg_dst_out, mem_wb_1_mem_to_reg_out, Reg_Write_EX, Reg_Write_MEM, Reg_Write_W;
  wire [1:0] hazard_unit_1_forward_a_ex, hazard_unit_1_forward_b_ex;
  wire [2:0] control_1_aluop, ex_mem_1_write_reg_out, id_ex_1_aluop_out, id_ex_1_rd_out, id_ex_1_rs_out,
       id_ex_1_rt_out, id_ex_1_shamt_out, mem_wb_1_write_reg_out, multiplexer_4_out, multiplexer_8_out;
  wire [11:0] if_id_1_instruction_out;
  wire [15:0] adder_1_out, adder_2_out, alu_1_result, ex_mem_1_alu_result_out, ex_mem_1_write_data_out,
       id_ex_1_immediate_out, id_ex_1_reg_data_1_out, id_ex_1_reg_data_2_out, if_id_1_pc_plus_out,
       mem_wb_1_alu_result_out, mem_wb_1_read_data_out, multiplexer_1_out, multiplexer_2_out,
       multiplexer_3_out, multiplexer_5_out, multiplexer_6_out, multiplexer_7_out, multiplexer_9_out,
       multiplexer_10_out, multiplexer_11_out, multiplexer_12_out, ram_1_dout, register_1_q,
       registers_1_regdata1, registers_1_regdata2, rom_1_data, sign_extend_1_out_2;
  wire [15:12] if_id_1_instruction_out_2;

  Multiplexer #(.width(16)) multiplexer_1 (
    .in0(adder_1_out), .in1(adder_2_out), .out(multiplexer_1_out), .sel(equal_checker_branch_1_branch));
  Multiplexer #(.width(16)) multiplexer_2 (
    .in0(multiplexer_1_out), .in1(multiplexer_3_out), .out(multiplexer_2_out), .sel(control_1_jump));
  Multiplexer #(.width(16)) multiplexer_3 (
    .in0({4'b0000, if_id_1_instruction_out}), .in1(registers_1_regdata1), .out(multiplexer_3_out),
    .sel(control_1_jr));
  Hazard_Unit hazard_unit_1 (
    .Clk_In(clock_1_out), .Sig_Reg_Write_MEM(Reg_Write_MEM), .Sig_Reg_Write_W(Reg_Write_W),
    .Sig_Reg_Write_EX(Reg_Write_EX), .Write_Reg_W(mem_wb_1_write_reg_out),
    .Sig_Branch_Jump_In(Branch_Jump_Stall), .Rs_EX(id_ex_1_rs_out), .Rt_EX(id_ex_1_rt_out),
    .Write_Reg_EX(multiplexer_8_out), .Rs_ID(if_id_1_instruction_out[11:9]),
    .Rt_ID(if_id_1_instruction_out[8:6]), .Write_Reg_MEM(ex_mem_1_write_reg_out),
    .Forward_A_EX(hazard_unit_1_forward_a_ex), .Forward_B_EX(hazard_unit_1_forward_b_ex),
    .Forwards_A_ID(hazard_unit_1_forwards_a_id), .Forward_B_ID(hazard_unit_1_forward_b_id),
    .Stall_EX(hazard_unit_1_stall_ex), .Stall_ID(hazard_unit_1_stall_id), .Stall_IF(hazard_unit_1_stall_if));
  Clock clock_1 (.out(clock_1_out));
  Register #(.width(16)) register_1 (
    .D(multiplexer_2_out), .en(hazard_unit_1_stall_if), .Q(register_1_q), .clk(clock_1_out));  // open: clr
  ROM #(.addrWidth(16), .dataWidth(16)) rom_1 (.addr(register_1_q), .data(rom_1_data));
  Adder #(.width(16)) adder_1 (.a(register_1_q), .b(16'h1), .out(adder_1_out));  // open: cin, cout
  IF_ID if_id_1 (
    .PC_Plus_In(adder_1_out), .Instruction_In(rom_1_data), .Enable(hazard_unit_1_stall_id),
    .Clk(clock_1_out), .PC_Plus_Out(if_id_1_pc_plus_out),
    .Instruction_Out({if_id_1_instruction_out_2, if_id_1_instruction_out}));
  Control control_1 (
    .Opcode({if_id_1_instruction_out_2, if_id_1_instruction_out}), .ALUOp(control_1_aluop),
    .Jr(control_1_jr), .BranchNe(control_1_branchne), .Branch(control_1_branch), .Jump(control_1_jump),
    .MemtoReg(control_1_memtoreg), .MemWrite(control_1_memwrite), .MemRead(control_1_memread),
    .ALUSrc(control_1_alusrc), .RegWrite(control_1_regwrite), .RegDst(control_1_regdst), .Jal(control_1_jal));
  Sign_Extend sign_extend_1 (.in_1(if_id_1_instruction_out[5:0]), .out_2(sign_extend_1_out_2));
  Multiplexer #(.width(3)) multiplexer_4 (
    .in0(mem_wb_1_write_reg_out), .in1(3'b111), .out(multiplexer_4_out), .sel(control_1_jal));
  Multiplexer #(.width(16)) multiplexer_5 (
    .in0(multiplexer_12_out), .in1(if_id_1_pc_plus_out), .out(multiplexer_5_out), .sel(control_1_jal));
  Adder #(.width(16)) adder_2 (.a(sign_extend_1_out_2), .b(if_id_1_pc_plus_out), .out(adder_2_out));  // open: cin, cout
  Registers registers_1 (
    .Clk(clock_1_out), .RegWrite(Reg_Write_W), .ReadAddress1(if_id_1_instruction_out[11:9]),
    .ReadAddress2(if_id_1_instruction_out[8:6]), .WriteAddress(multiplexer_4_out),
    .Data_Input(multiplexer_5_out), .zero(zero), .r0(r0), .r1(r1), .r2(r2), .r3(r3), .r4(r4), .r5(r5),
    .ra(ra), .RegData1(registers_1_regdata1), .RegData2(registers_1_regdata2));
  or or_1 (Branch_Jump_Stall, control_1_branch, Reg_Write_W);
  Multiplexer #(.width(16)) multiplexer_6 (
    .in0(registers_1_regdata1), .in1(ex_mem_1_alu_result_out), .out(multiplexer_6_out),
    .sel(hazard_unit_1_forwards_a_id));
  Multiplexer #(.width(16)) multiplexer_7 (
    .in0(registers_1_regdata2), .in1(ex_mem_1_alu_result_out), .out(multiplexer_7_out),
    .sel(hazard_unit_1_forward_b_id));
  ID_EX id_ex_1 (
    .Reg_Write_In(control_1_regwrite), .Mem_to_Reg_In(control_1_memtoreg), .Mem_Write_In(control_1_memwrite),
    .Mem_Read_In(control_1_memread), .ALU_Src_In(control_1_alusrc), .Reg_Dst_In(control_1_regdst),
    .ALUOp_In(control_1_aluop), .Shamt_In(if_id_1_instruction_out[8:6]),
    .Rt_In(if_id_1_instruction_out[8:6]), .Rd_In(if_id_1_instruction_out[5:3]),
    .Rs_In(if_id_1_instruction_out[11:9]), .Reg_Data_1_In(multiplexer_6_out),
    .Reg_Data_2_In(multiplexer_7_out), .Immediate_In(sign_extend_1_out_2), .Enable(hazard_unit_1_stall_ex),
    .Clk(clock_1_out), .Reg_Write_Out(Reg_Write_EX), .Mem_to_Reg_Out(id_ex_1_mem_to_reg_out),
    .Mem_Write_Out(id_ex_1_mem_write_out), .Mem_Read_Out(id_ex_1_mem_read_out),
    .ALUOp_Out(id_ex_1_aluop_out), .ALU_Src_Out(id_ex_1_alu_src_out), .Reg_Dst_Out(id_ex_1_reg_dst_out),
    .Shamt_Out(id_ex_1_shamt_out), .Reg_Data_1_Out(id_ex_1_reg_data_1_out),
    .Reg_Data_2_Out(id_ex_1_reg_data_2_out), .Rt_Out(id_ex_1_rt_out), .Rd_Out(id_ex_1_rd_out),
    .Rs_Out(id_ex_1_rs_out), .Immediate_Out(id_ex_1_immediate_out));
  Equal_Checker_Branch equal_checker_branch_1 (
    .Sig_Branch_Ne(control_1_branchne), .Sig_Branch(control_1_branch), .in_3(multiplexer_6_out),
    .in_4(multiplexer_7_out), .Branch(equal_checker_branch_1_branch));
  Multiplexer #(.width(3)) multiplexer_8 (
    .in0(id_ex_1_rt_out), .in1(id_ex_1_rd_out), .out(multiplexer_8_out), .sel(id_ex_1_reg_dst_out));
  Multiplexer #(.select(2), .width(16)) multiplexer_9 (
    .in0(id_ex_1_reg_data_1_out), .in1(multiplexer_12_out), .in2(ex_mem_1_alu_result_out),
    .out(multiplexer_9_out), .sel(hazard_unit_1_forward_a_ex));  // open: in3
  Multiplexer #(.select(2), .width(16)) multiplexer_10 (
    .in0(id_ex_1_reg_data_2_out), .in1(multiplexer_12_out), .in2(ex_mem_1_alu_result_out),
    .out(multiplexer_10_out), .sel(hazard_unit_1_forward_b_ex));  // open: in3
  Multiplexer #(.width(16)) multiplexer_11 (
    .in0(multiplexer_10_out), .in1(id_ex_1_immediate_out), .out(multiplexer_11_out), .sel(id_ex_1_alu_src_out));
  EX_MEM ex_mem_1 (
    .Reg_Write_In(Reg_Write_EX), .Mem_to_Reg_In(id_ex_1_mem_to_reg_out),
    .Mem_Write_In(id_ex_1_mem_write_out), .Mem_Read_In(id_ex_1_mem_read_out),
    .Write_Reg_In(multiplexer_8_out), .ALU_Result_In(alu_1_result), .Write_Data_In(multiplexer_10_out),
    .Clk(clock_1_out), .Reg_Write_Out(Reg_Write_MEM), .Mem_to_Reg_Out(ex_mem_1_mem_to_reg_out),
    .Mem_Write_Out(ex_mem_1_mem_write_out), .Mem_Read_Out(ex_mem_1_mem_read_out),
    .ALU_Result_Out(ex_mem_1_alu_result_out), .Write_Data_Out(ex_mem_1_write_data_out),
    .Write_Reg_Out(ex_mem_1_write_reg_out));
  ALU alu_1 (
    .ALUOp(id_ex_1_shamt_out), .Operand1(multiplexer_9_out), .Operand2(multiplexer_11_out),
    .Shamt(id_ex_1_aluop_out), .Result(alu_1_result));
  RAM #(.addrWidth(16), .dataWidth(16), .trigger("falling"), .\type ("nonvolatile")) ram_1 (
    .addr(ex_mem_1_alu_result_out), .we(ex_mem_1_mem_write_out), .oe(ex_mem_1_mem_read_out),
    .clk(clock_1_out), .din(ex_mem_1_write_data_out), .dout(ram_1_dout));
  MEM_WB mem_wb_1 (
    .Reg_Write_In(Reg_Write_MEM), .Mem_to_Reg_In(ex_mem_1_mem_to_reg_out),
    .Write_Reg_In(ex_mem_1_write_reg_out), .Read_Data_In(ram_1_dout),
    .ALU_Result_In(ex_mem_1_alu_result_out), .Clk(clock_1_out), .Reg_Write_Out(Reg_Write_W),
    .Mem_to_Reg_Out(mem_wb_1_mem_to_reg_out), .Read_Data_Out(mem_wb_1_read_data_out),
    .ALU_Result_Out(mem_wb_1_alu_result_out), .Write_Reg_Out(mem_wb_1_write_reg_out));
  Multiplexer #(.disabled("Z"), .width(16)) multiplexer_12 (
    .in0(mem_wb_1_alu_result_out), .in1(mem_wb_1_read_data_out), .out(multiplexer_12_out),
    .sel(mem_wb_1_mem_to_reg_out));

  // Notes on the sheet:
  //   contents of rom_1 (hex, n*v repeats v):
  //   2041 2280
endmodule

module IF_ID (
  input  [15:0] PC_Plus_In,
  input  [15:0] Instruction_In,
  input  Enable,
  input  Clk,
  output [15:0] PC_Plus_Out,
  output [15:0] Instruction_Out
);

  Register #(.width(16)) register_1 (.D(PC_Plus_In), .en(Enable), .Q(PC_Plus_Out), .clk(Clk));  // open: clr
  Register #(.width(16)) register_2 (.D(Instruction_In), .en(Enable), .Q(Instruction_Out), .clk(Clk));  // open: clr
endmodule

module Equal_Checker_Branch (
  input  Sig_Branch_Ne,
  input  Sig_Branch,
  input  [15:0] in_3,
  input  [15:0] in_4,
  output Branch
);

  wire equal_checker_16bit_1_zero, multiplexer_1_out, not_1_out;
  wire [15:0] xor_1_out;

  assign xor_1_out = in_3 ^ in_4;  // XOR_Gate xor_1, 16 bits wide
  Equal_Checker_16bit equal_checker_16bit_1 (.bits(xor_1_out), .Zero(equal_checker_16bit_1_zero));
  not not_1 (not_1_out, equal_checker_16bit_1_zero);
  Multiplexer multiplexer_1 (
    .in0(equal_checker_16bit_1_zero), .in1(not_1_out), .out(multiplexer_1_out), .sel(Sig_Branch_Ne));
  and and_1 (Branch, Sig_Branch, multiplexer_1_out);
endmodule

module ID_EX (
  input  Reg_Write_In,
  input  Mem_to_Reg_In,
  input  Mem_Write_In,
  input  Mem_Read_In,
  input  [2:0] ALUOp_In,
  input  ALU_Src_In,
  input  Reg_Dst_In,
  input  [2:0] Shamt_In,
  input  [15:0] Reg_Data_1_In,
  input  [15:0] Reg_Data_2_In,
  input  [2:0] Rs_In,
  input  [2:0] Rt_In,
  input  [2:0] Rd_In,
  input  [15:0] Immediate_In,
  input  Enable,
  input  Clk,
  output Reg_Write_Out,
  output Mem_to_Reg_Out,
  output Mem_Write_Out,
  output Mem_Read_Out,
  output [2:0] ALUOp_Out,
  output ALU_Src_Out,
  output Reg_Dst_Out,
  output [2:0] Shamt_Out,
  output [15:0] Reg_Data_1_Out,
  output [15:0] Reg_Data_2_Out,
  output [2:0] Rs_Out,
  output [2:0] Rt_Out,
  output [2:0] Rd_Out,
  output [15:0] Immediate_Out
);

  Register #(.width(1)) register_1 (.D(Reg_Write_In), .en(Enable), .Q(Reg_Write_Out), .clk(Clk));  // open: clr
  Register #(.width(1)) register_2 (.D(Mem_to_Reg_In), .en(Enable), .Q(Mem_to_Reg_Out), .clk(Clk));  // open: clr
  Register #(.width(1)) register_3 (.D(Mem_Write_In), .en(Enable), .Q(Mem_Write_Out), .clk(Clk));  // open: clr
  Register #(.width(1)) register_4 (.D(Mem_Read_In), .en(Enable), .Q(Mem_Read_Out), .clk(Clk));  // open: clr
  Register #(.width(3)) register_5 (.D(ALUOp_In), .en(Enable), .Q(ALUOp_Out), .clk(Clk));  // open: clr
  Register #(.width(1)) register_6 (.D(ALU_Src_In), .en(Enable), .Q(ALU_Src_Out), .clk(Clk));  // open: clr
  Register #(.width(1)) register_7 (.D(Reg_Dst_In), .en(Enable), .Q(Reg_Dst_Out), .clk(Clk));  // open: clr
  Register #(.width(3)) register_8 (.D(Shamt_In), .en(Enable), .Q(Shamt_Out), .clk(Clk));  // open: clr
  Register #(.width(16)) register_9 (.D(Reg_Data_1_In), .en(Enable), .Q(Reg_Data_1_Out), .clk(Clk));  // open: clr
  Register #(.width(16)) register_10 (.D(Reg_Data_2_In), .en(Enable), .Q(Reg_Data_2_Out), .clk(Clk));  // open: clr
  Register #(.width(3)) register_11 (.D(Rs_In), .en(Enable), .Q(Rs_Out), .clk(Clk));  // open: clr
  Register #(.width(3)) register_12 (.D(Rt_In), .en(Enable), .Q(Rt_Out), .clk(Clk));  // open: clr
  Register #(.width(3)) register_13 (.D(Rd_In), .en(Enable), .Q(Rd_Out), .clk(Clk));  // open: clr
  Register #(.width(16)) register_14 (.D(Immediate_In), .en(Enable), .Q(Immediate_Out), .clk(Clk));  // open: clr
endmodule

module EX_MEM (
  input  Reg_Write_In,
  input  Mem_to_Reg_In,
  input  Mem_Write_In,
  input  Mem_Read_In,
  input  [15:0] ALU_Result_In,
  input  [15:0] Write_Data_In,
  input  [2:0] Write_Reg_In,
  input  Clk,
  output Reg_Write_Out,
  output Mem_to_Reg_Out,
  output Mem_Write_Out,
  output Mem_Read_Out,
  output [15:0] ALU_Result_Out,
  output [15:0] Write_Data_Out,
  output [2:0] Write_Reg_Out
);

  Register #(.width(1)) register_1 (.D(Reg_Write_In), .en(Clk), .Q(Reg_Write_Out), .clk(Clk));  // open: clr
  Register #(.width(1)) register_2 (.D(Mem_to_Reg_In), .en(Clk), .Q(Mem_to_Reg_Out), .clk(Clk));  // open: clr
  Register #(.width(1)) register_3 (.D(Mem_Write_In), .en(Clk), .Q(Mem_Write_Out), .clk(Clk));  // open: clr
  Register #(.width(1)) register_4 (.D(Mem_Read_In), .en(Clk), .Q(Mem_Read_Out), .clk(Clk));  // open: clr
  Register #(.width(16)) register_5 (.D(ALU_Result_In), .en(Clk), .Q(ALU_Result_Out), .clk(Clk));  // open: clr
  Register #(.width(16)) register_6 (.D(Write_Data_In), .en(Clk), .Q(Write_Data_Out), .clk(Clk));  // open: clr
  Register #(.width(3)) register_7 (.D(Write_Reg_In), .en(Clk), .Q(Write_Reg_Out), .clk(Clk));  // open: clr
endmodule

module MEM_WB (
  input  Reg_Write_In,
  input  Mem_to_Reg_In,
  input  [15:0] Read_Data_In,
  input  [15:0] ALU_Result_In,
  input  [2:0] Write_Reg_In,
  input  Clk,
  output Reg_Write_Out,
  output Mem_to_Reg_Out,
  output [15:0] Read_Data_Out,
  output [15:0] ALU_Result_Out,
  output [2:0] Write_Reg_Out
);

  Register #(.width(1)) register_1 (.D(Reg_Write_In), .en(Clk), .Q(Reg_Write_Out), .clk(Clk));  // open: clr
  Register #(.width(1)) register_2 (.D(Mem_to_Reg_In), .en(Clk), .Q(Mem_to_Reg_Out), .clk(Clk));  // open: clr
  Register #(.width(16)) register_3 (.D(Read_Data_In), .en(Clk), .Q(Read_Data_Out), .clk(Clk));  // open: clr
  Register #(.width(16)) register_4 (.D(ALU_Result_In), .en(Clk), .Q(ALU_Result_Out), .clk(Clk));  // open: clr
  Register #(.width(3)) register_5 (.D(Write_Reg_In), .en(Clk), .Q(Write_Reg_Out), .clk(Clk));  // open: clr
endmodule

module Control_Nope (
  input  [15:0] Instruction,
  output Nope
);

  or or_1 (Nope, Instruction[0], Instruction[1], Instruction[2], Instruction[3], Instruction[4], Instruction[5], Instruction[6], Instruction[7], Instruction[9], Instruction[10], Instruction[11], Instruction[12], Instruction[13], Instruction[14], Instruction[15], Instruction[8]);
endmodule

// Hazard Unit
module Hazard_Unit (
  input  Sig_Branch_Jump_In,
  input  [2:0] Write_Reg_EX,
  input  Sig_Reg_Write_EX,
  input  [2:0] Rs_ID,
  input  [2:0] Rt_ID,
  input  [2:0] Write_Reg_MEM,
  input  Sig_Reg_Write_MEM,
  input  [2:0] Rs_EX,
  input  [2:0] Rt_EX,
  input  [2:0] Write_Reg_W,
  input  Sig_Reg_Write_W,
  input  Clk_In,
  output Stall_IF,
  output Stall_ID,
  output Forwards_A_ID,
  output Forward_B_ID,
  output [1:0] Forward_A_EX,
  output [1:0] Forward_B_EX,
  output Stall_EX
);

  wire and_1_out, and_2_out, and_3_out, and_4_out, and_5_out, and_6_out, bitselector_6_out,
       equal_checker_3bit_1_zero, equal_checker_3bit_2_zero, equal_checker_3bit_3_zero,
       equal_checker_3bit_4_zero, equal_checker_3bit_5_zero, equal_checker_3bit_6_zero, multiplexer_1_out,
       not_1_out, not_2_out, not_3_out, not_4_out, not_5_out, not_6_out, or_1_out, register_1_q,
       register_4_q, register_5_q;
  wire [1:0] bitselector_1_out, bitselector_2_out, bitselector_3_out, bitselector_4_out;
  wire [2:0] xor_1_out, xor_2_out, xor_3_out, xor_4_out, xor_5_out, xor_6_out;

  Register #(.width(1)) register_1 (.D(Sig_Branch_Jump_In), .en(Clk_In), .Q(register_1_q), .clk(Clk_In));  // open: clr
  assign xor_1_out = Write_Reg_EX ^ Rs_ID;  // XOR_Gate xor_1, 3 bits wide
  Equal_Checker_3bit equal_checker_3bit_1 (.bits(xor_1_out), .Zero(equal_checker_3bit_1_zero));
  assign xor_2_out = Write_Reg_EX ^ Rt_ID;  // XOR_Gate xor_2, 3 bits wide
  Equal_Checker_3bit equal_checker_3bit_2 (.bits(xor_2_out), .Zero(equal_checker_3bit_2_zero));
  assign xor_3_out = Write_Reg_MEM ^ Rs_EX;  // XOR_Gate xor_3, 3 bits wide
  assign xor_4_out = Write_Reg_MEM ^ Rt_EX;  // XOR_Gate xor_4, 3 bits wide
  assign xor_5_out = Write_Reg_W ^ Rs_EX;  // XOR_Gate xor_5, 3 bits wide
  assign xor_6_out = Write_Reg_W ^ Rt_EX;  // XOR_Gate xor_6, 3 bits wide
  Equal_Checker_3bit equal_checker_3bit_3 (.bits(xor_3_out), .Zero(equal_checker_3bit_3_zero));
  Equal_Checker_3bit equal_checker_3bit_4 (.bits(xor_4_out), .Zero(equal_checker_3bit_4_zero));
  Equal_Checker_3bit equal_checker_3bit_5 (.bits(xor_5_out), .Zero(equal_checker_3bit_5_zero));
  Equal_Checker_3bit equal_checker_3bit_6 (.bits(xor_6_out), .Zero(equal_checker_3bit_6_zero));
  and and_1 (and_1_out, Sig_Reg_Write_EX, equal_checker_3bit_1_zero);
  and and_2 (and_2_out, Sig_Reg_Write_EX, equal_checker_3bit_2_zero);
  and and_3 (and_3_out, Sig_Reg_Write_MEM, equal_checker_3bit_3_zero);
  and and_4 (and_4_out, Sig_Reg_Write_MEM, equal_checker_3bit_4_zero);
  and and_5 (and_5_out, Sig_Reg_Write_W, equal_checker_3bit_5_zero);
  and and_6 (and_6_out, Sig_Reg_Write_W, equal_checker_3bit_6_zero);
  Register #(.width(1)) register_2 (.D(and_1_out), .en(Clk_In), .Q(Forwards_A_ID), .clk(Clk_In));  // open: clr
  Register #(.width(1)) register_3 (.D(and_2_out), .Q(Forward_B_ID), .clk(Clk_In));  // open: en, clr
  not not_1 (not_1_out, and_3_out);
  not not_2 (not_2_out, and_4_out);
  Register #(.width(1)) register_4 (.D(and_5_out), .en(Clk_In), .Q(register_4_q), .clk(Clk_In));  // open: clr
  Register #(.width(1)) register_5 (.D(and_6_out), .en(Clk_In), .Q(register_5_q), .clk(Clk_In));  // open: clr
  BitSelector #(.group(2), .width(2)) bitselector_1 (.in(2'b10), .out(bitselector_1_out), .sel(not_1_out));
  BitSelector #(.group(2), .width(2)) bitselector_2 (.in(2'b10), .out(bitselector_2_out), .sel(not_2_out));
  not not_3 (not_3_out, register_4_q);
  not not_4 (not_4_out, register_5_q);
  not not_5 (not_5_out, register_1_q);
  not not_6 (not_6_out, and_1_out);
  not not_7 (Stall_EX, and_5_out);
  BitSelector #(.group(2), .width(2)) bitselector_3 (.in(2'b01), .out(bitselector_3_out), .sel(not_3_out));
  BitSelector #(.group(2), .width(2)) bitselector_4 (.in(2'b01), .out(bitselector_4_out), .sel(not_4_out));
  Multiplexer multiplexer_1 (.in0(not_5_out), .in1(1'b1), .out(multiplexer_1_out), .sel(or_1_out));
  or or_1 (or_1_out, Forwards_A_ID, Forward_B_ID);
  Multiplexer #(.width(2)) multiplexer_2 (
    .in0(bitselector_1_out), .in1(bitselector_3_out), .out(Forward_A_EX), .sel(register_4_q));
  Multiplexer #(.width(2)) multiplexer_3 (
    .in0(bitselector_2_out), .in1(bitselector_4_out), .out(Forward_B_EX), .sel(register_4_q));
  BitSelector #(.width(1)) bitselector_5 (.in(not_6_out), .out(Stall_ID), .sel(and_5_out));
  BitSelector #(.width(1)) bitselector_6 (.in(multiplexer_1_out), .out(bitselector_6_out), .sel(and_1_out));
  BitSelector #(.width(1)) bitselector_7 (.in(bitselector_6_out), .out(Stall_IF), .sel(and_5_out));
endmodule

module Equal_Checker_3bit (
  input  [2:0] bits,
  output Zero
);

  wire or_1_out;

  or or_1 (or_1_out, bits[0], bits[1], bits[2]);
  not not_1 (Zero, or_1_out);
endmodule
