// Logisim project MIPS_Singlecycle.circ as structural Verilog: 11 circuits, main circuit ALU
module ALU (
  input  [2:0] ALUOp,
  input  [15:0] Operand1,
  input  [15:0] Operand2,
  input  [2:0] Shamt,
  output [15:0] Result,
  output Zero
);

  wire [0:0] subtractor_1_out_2;
  wire [14:0] subtractor_1_out;
  wire [15:0] adder_1_out, and_1_out, or_1_out, shifter_1_out, shifter_2_out;

  Adder #(.width(16)) adder_1 (.a(Operand1), .b(Operand2), .out(adder_1_out));  // open: cin, cout
  Subtractor #(.width(16)) subtractor_1 (
    .a(Operand1), .b(Operand2), .out({subtractor_1_out_2[0], subtractor_1_out}));  // open: bin, bout
  assign and_1_out = Operand1 & Operand2;  // AND_Gate and_1, 16 bits wide
  assign or_1_out = Operand1 | Operand2;  // OR_Gate or_1, 16 bits wide
  Shifter #(.width(16)) shifter_1 (.in(Operand1), .\dist ({1'b0, Shamt}), .out(shifter_1_out));
  Shifter #(.shift("lr"), .width(16)) shifter_2 (.in(Operand1), .\dist ({1'b0, Shamt}), .out(shifter_2_out));
  Multiplexer #(.select(3), .width(16)) multiplexer_1 (
    .in0(adder_1_out), .in1({subtractor_1_out_2[0], subtractor_1_out}), .in2(and_1_out), .in3(or_1_out),
    .in4(shifter_1_out), .in5(shifter_2_out), .in6({{15{1'b0}}, subtractor_1_out_2[0]}), .out(Result),
    .sel(ALUOp));  // open: in7
  Equal_Checker equal_checker_1 (.bits({subtractor_1_out_2[0], subtractor_1_out}), .Zero(Zero));
endmodule

module Equal_Checker (
  input  [15:0] bits,
  output Zero
);

  wire or_1_out;

  or or_1 (or_1_out, bits[0], bits[1], bits[2], bits[3], bits[4], bits[5], bits[6], bits[7], bits[9], bits[10], bits[11], bits[12], bits[13], bits[14], bits[15], bits[8]);
  not not_1 (Zero, or_1_out);
endmodule

module Registers (
  input  RegWrite,
  input  [2:0] ReadAddress1,
  input  [2:0] ReadAddress2,
  input  [2:0] WriteAddress,
  input  [15:0] Data_Input,
  input  Clk,
  output [15:0] RegData1,
  output [15:0] RegData2,
  output [15:0] zero,
  output [15:0] r0,
  output [15:0] r1,
  output [15:0] r2,
  output [15:0] r3,
  output [15:0] r4,
  output [15:0] r5,
  output [15:0] ra
);

  wire demultiplexer_1_out0, demultiplexer_1_out1, demultiplexer_1_out2, demultiplexer_1_out3,
       demultiplexer_1_out4, demultiplexer_1_out5, demultiplexer_1_out6, demultiplexer_1_out7;

  Demultiplexer #(.select(3)) demultiplexer_1 (
    .out0(demultiplexer_1_out0), .out1(demultiplexer_1_out1), .out2(demultiplexer_1_out2),
    .out3(demultiplexer_1_out3), .out4(demultiplexer_1_out4), .out5(demultiplexer_1_out5),
    .out6(demultiplexer_1_out6), .out7(demultiplexer_1_out7), .in(RegWrite), .sel(WriteAddress));
  Register #(.width(16)) register_1 (.D(Data_Input), .en(demultiplexer_1_out0), .Q(zero), .clk(Clk));  // open: clr
  Register #(.width(16)) register_2 (.D(Data_Input), .en(demultiplexer_1_out1), .Q(r0), .clk(Clk));  // open: clr
  Register #(.width(16)) register_3 (.D(Data_Input), .en(demultiplexer_1_out2), .Q(r1), .clk(Clk));  // open: clr
  Register #(.width(16)) register_4 (.D(Data_Input), .en(demultiplexer_1_out3), .Q(r2), .clk(Clk));  // open: clr
  Register #(.width(16)) register_5 (.D(Data_Input), .en(demultiplexer_1_out4), .Q(r3), .clk(Clk));  // open: clr
  Register #(.width(16)) register_6 (.D(Data_Input), .en(demultiplexer_1_out5), .Q(r4), .clk(Clk));  // open: clr
  Register #(.width(16)) register_7 (.D(Data_Input), .en(demultiplexer_1_out6), .Q(r5), .clk(Clk));  // open: clr
  Register #(.width(16)) register_8 (.D(Data_Input), .en(demultiplexer_1_out7), .Q(ra), .clk(Clk));  // open: clr
  Multiplexer #(.select(3), .width(16)) multiplexer_1 (
    .in0(zero), .in1(r0), .in2(r1), .in3(r2), .in4(r3), .in5(r4), .in6(r5), .in7(ra), .out(RegData1),
    .sel(ReadAddress1));
  Multiplexer #(.select(3), .width(16)) multiplexer_2 (
    .in0(zero), .in1(r0), .in2(r1), .in3(r2), .in4(r3), .in5(r4), .in6(r5), .in7(ra), .out(RegData2),
    .sel(ReadAddress2));
endmodule

module MIPS_Single_Cycle (
  output [15:0] zero,
  output [15:0] r0,
  output [15:0] r1,
  output [15:0] r2,
  output [15:0] r3,
  output [15:0] r4,
  output [15:0] r5,
  output [15:0] ra
);

  wire alu_1_zero, and_1_out, clock_1_out, control_1_alusrc, control_1_branch, control_1_branchne,
       control_1_jal, control_1_jr, control_1_jump, control_1_memread, control_1_memtoreg,
       control_1_memwrite, control_1_regdst, control_1_regwrite, multiplexer_7_out, not_1_out,
       rom_enable_1_enable;
  wire [2:0] control_1_aluop, multiplexer_1_out, multiplexer_3_out;
  wire [3:0] adder_1_out;
  wire [11:0] adder_1_out_2;
  wire [15:0] adder_2_out, alu_1_result, multiplexer_2_out, multiplexer_4_out, multiplexer_5_out,
       multiplexer_6_out, multiplexer_8_out, multiplexer_9_out, ram_1_dout, register_1_q,
       registers_1_regdata1, registers_1_regdata2, rom_1_data, sign_extend_1_out_2;

  Clock clock_1 (.out(clock_1_out));
  Register #(.width(16)) register_1 (.D(multiplexer_8_out), .Q(register_1_q), .clk(clock_1_out));  // open: en, clr
  ROM #(.addrWidth(16), .dataWidth(16)) rom_1 (.addr(register_1_q), .data(rom_1_data));
  Adder #(.width(16)) adder_1 (.a(register_1_q), .b(16'h1), .out({adder_1_out, adder_1_out_2}));  // open: cin, cout
  Control control_1 (
    .Opcode(rom_1_data), .ALUOp(control_1_aluop), .Jr(control_1_jr), .BranchNe(control_1_branchne),
    .Branch(control_1_branch), .Jump(control_1_jump), .MemtoReg(control_1_memtoreg),
    .MemWrite(control_1_memwrite), .MemRead(control_1_memread), .ALUSrc(control_1_alusrc),
    .RegWrite(control_1_regwrite), .RegDst(control_1_regdst), .Jal(control_1_jal));
  Multiplexer #(.width(3)) multiplexer_1 (
    .in0(rom_1_data[8:6]), .in1(3'b111), .out(multiplexer_1_out), .sel(control_1_jal));
  Multiplexer #(.width(16)) multiplexer_2 (
    .in0(multiplexer_9_out), .in1({adder_1_out, adder_1_out_2}), .out(multiplexer_2_out), .sel(control_1_jal));
  Multiplexer #(.width(3)) multiplexer_3 (
    .in0(multiplexer_1_out), .in1(rom_1_data[5:3]), .out(multiplexer_3_out), .sel(control_1_regdst));
  Registers registers_1 (
    .Clk(clock_1_out), .RegWrite(control_1_regwrite), .ReadAddress1(rom_1_data[11:9]),
    .ReadAddress2(rom_1_data[8:6]), .WriteAddress(multiplexer_3_out), .Data_Input(multiplexer_2_out),
    .zero(zero), .r0(r0), .r1(r1), .r2(r2), .r3(r3), .r4(r4), .r5(r5), .ra(ra),
    .RegData1(registers_1_regdata1), .RegData2(registers_1_regdata2));
  Sign_Extend sign_extend_1 (.in_1(rom_1_data[5:0]), .out_2(sign_extend_1_out_2));
  Multiplexer #(.width(16)) multiplexer_4 (
    .in0({adder_1_out, rom_1_data[11:0]}), .in1(registers_1_regdata1), .out(multiplexer_4_out),
    .sel(control_1_jr));
  Multiplexer #(.width(16)) multiplexer_5 (
    .in0(registers_1_regdata2), .in1(sign_extend_1_out_2), .out(multiplexer_5_out), .sel(control_1_alusrc));
  not not_1 (not_1_out, alu_1_zero);
  ALU alu_1 (
    .ALUOp(control_1_aluop), .Operand1(registers_1_regdata1), .Operand2(multiplexer_5_out),
    .Shamt(rom_1_data[8:6]), .Result(alu_1_result), .Zero(alu_1_zero));
  Multiplexer #(.width(16)) multiplexer_6 (
    .in0({adder_1_out, adder_1_out_2}), .in1(adder_2_out), .out(multiplexer_6_out), .sel(and_1_out));
  Adder #(.width(16)) adder_2 (
    .a({adder_1_out, adder_1_out_2}), .b(sign_extend_1_out_2), .out(adder_2_out));  // open: cin, cout
  Multiplexer multiplexer_7 (.in0(alu_1_zero), .in1(not_1_out), .out(multiplexer_7_out), .sel(control_1_branchne));
  and and_1 (and_1_out, multiplexer_7_out, control_1_branch);
  RAM #(.addrWidth(16), .dataWidth(16), .trigger("falling")) ram_1 (
    .addr(alu_1_result), .we(control_1_memwrite), .oe(control_1_memtoreg), .clk(rom_enable_1_enable),
    .din(registers_1_regdata2), .dout(ram_1_dout));
  ROM_Enable rom_enable_1 (
    .Write(clock_1_out), .Read(control_1_memtoreg), .Clk(control_1_memwrite), .Enable(rom_enable_1_enable));
  Multiplexer #(.width(16)) multiplexer_8 (
    .in0(multiplexer_6_out), .in1(multiplexer_4_out), .out(multiplexer_8_out), .sel(control_1_jump));
  Multiplexer #(.disabled("Z"), .width(16)) multiplexer_9 (
    .in0(alu_1_result), .in1(ram_1_dout), .out(multiplexer_9_out), .sel(control_1_memtoreg));

  // Notes on the sheet:
  //   contents of rom_1 (hex, n*v repeats v):
  //   1042 1085 10ca 3040 3081 30c2
endmodule

module Control (
  input  [15:0] Opcode,
  output Jr,
  output BranchNe,
  output Branch,
  output Jump,
  output MemtoReg,
  output MemWrite,
  output MemRead,
  output ALUSrc,
  output RegWrite,
  output RegDst,
  output Jal,
  output [2:0] ALUOp
);

  wire opcode_decoder_1_funct;
  wire [2:0] alu_decoder_1_aluop;

  Opcode_Decoder opcode_decoder_1 (
    .Opcode(Opcode[15:12]), .Jr(Jr), .BranchNe(BranchNe), .Branch(Branch), .Jump(Jump), .MemtoReg(MemtoReg),
    .MemWrite(MemWrite), .MemRead(MemRead), .ALUSrc(ALUSrc), .RegWrite(RegWrite), .RegDst(RegDst), .Jal(Jal),
    .Funct(opcode_decoder_1_funct));
  ALU_Decoder alu_decoder_1 (.Opcode(Opcode[15:12]), .ALUOp(alu_decoder_1_aluop));
  Multiplexer #(.width(3)) multiplexer_1 (
    .in0(alu_decoder_1_aluop), .in1(Opcode[2:0]), .out(ALUOp), .sel(opcode_decoder_1_funct));
endmodule

module PC (
  input  [15:0] OverWrite,
  input  Clk,
  output [15:0] InstructionAddress
);

  Register #(.width(16)) register_1 (.D(OverWrite), .Q(InstructionAddress), .clk(Clk));  // open: en, clr
endmodule

module ALU_Decoder (
  input  [3:0] Opcode,
  output [2:0] ALUOp
);

  wire and_1_out, not_1_out, not_2_out, not_3_out, not_4_out;

  not not_1 (not_1_out, Opcode[3]);
  not not_2 (not_2_out, Opcode[2]);
  not not_3 (not_3_out, Opcode[1]);
  not not_4 (not_4_out, Opcode[0]);
  and and_1 (and_1_out, not_4_out, not_3_out, not_2_out, not_1_out, 1'b0);
  or or_1 (ALUOp[0], and_1_out, Opcode[2]);
  or or_2 (ALUOp[1], and_1_out, and_1_out);
  or or_3 (ALUOp[2], and_1_out, and_1_out);
endmodule

module Opcode_Decoder (
  input  [3:0] Opcode,
  output Jr,
  output BranchNe,
  output Branch,
  output Jump,
  output MemtoReg,
  output MemWrite,
  output MemRead,
  output ALUSrc,
  output RegWrite,
  output RegDst,
  output Jal,
  output Funct
);

  wire and_8_out, not_1_out, not_2_out, not_3_out, not_4_out, not_5_out, not_6_out;

  not not_1 (not_1_out, Opcode[3]);
  not not_2 (not_2_out, Opcode[2]);
  not not_3 (not_3_out, Opcode[1]);
  not not_4 (not_4_out, Opcode[0]);
  and and_1 (Jr, not_4_out, Opcode[1], not_2_out, Opcode[3]);
  and and_2 (BranchNe, Opcode[0], not_3_out, Opcode[2], not_1_out);
  not not_5 (not_5_out, Opcode[2]);
  and and_3 (Jal, Opcode[0], not_3_out, not_2_out, Opcode[3]);
  and and_4 (MemWrite, Opcode[0], Opcode[1], not_2_out, not_1_out);
  and and_5 (MemRead, not_4_out, Opcode[1], not_2_out, not_1_out);
  not not_6 (not_6_out, Funct);
  and and_6 (Funct, not_4_out, not_3_out, not_2_out, not_1_out);
  and and_7 (ALUSrc, not_1_out, not_5_out, not_6_out);
  and and_8 (and_8_out, Opcode[0], not_3_out, not_2_out, not_1_out);
  or or_1 (RegWrite, and_8_out, Jal, MemRead, Funct);

  assign Branch = Opcode[2];
  assign Jump = Opcode[3];
  assign MemtoReg = MemRead;
  assign RegDst = Funct;
endmodule

module Sign_Extend (
  input  [5:0] in_1,
  output [15:0] out_2
);


  assign out_2 = {{11{in_1[5]}}, in_1[4:0]};
endmodule

module Twos_Complement (
  input  [15:0] in_1,
  output [15:0] out_2
);

  Negator #(.width(16)) negator_1 (.in(in_1), .out(out_2));
endmodule

module ROM_Enable (
  input  Write,
  input  Read,
  input  Clk,
  output Enable
);

  wire and_1_out, and_2_out;

  and and_1 (and_1_out, Write, Clk);
  and and_2 (and_2_out, Read, Clk);
  or or_1 (Enable, and_1_out, and_2_out);
endmodule
